# Fritzing sketch Untitled_Sketch (saved by Fritzing 0.9.3b)

parts:
  Composant1 = Arduino Uno (Rev3)  # not connected
  Composant2 = Base Shield V2
  Grove1 = Grove Temperature Sensor
  Grove2 = Grove OLED 128x96
  Grove3 = Grove 4 Digit Display

nets:
  N1: Composant2.pin_96, Grove3.GND
  N2: Composant2.pin_97, Grove3.VCC
  N3: Composant2.pin_98, Grove3.DIO
  N4: Composant2.pin_99, Grove3.CLK
  N5: Composant2.pin_124, Grove2.GND
  N6: Composant2.pin_125, Grove2.VCC
  N7: Composant2.pin_126, Grove2.SDA
  N8: Composant2.pin_127, Grove2.SCL
  N9: Composant2.pin_140, Grove1.SIG
  N10: Composant2.pin_142, Grove1.VCC
  N11: Composant2.pin_143, Grove1.GND
